// Logisim project T1.circ as structural Verilog: 1 circuit, main circuit main
module main (
  input  A,
  input  in_2,
  input  B,
  input  in_4,
  input  A_2,
  input  B_2,
  input  A_3,
  input  A_4,
  input  B_3,
  input  C,
  input  A_5,
  input  B_4,
  input  A_6,
  input  B_5,
  input  A_7,
  input  B_6,
  output SUM,
  output Y,
  output CARRY,
  output Y_2,
  output Y_3,
  output SUM_2,
  output Y_4,
  output Y_5,
  output CARRY_2,
  output Y_6
);

  wire and_3_out, and_4_out, and_5_out, or_2_out, xor_3_out;

  and and_1 (Y, in_2, in_4);
  or or_1 (Y_2, A_2, B_2);
  not not_1 (Y_3, A_4);
  nand nand_1 (Y_4, A_5, B_4);
  nor nor_1 (Y_5, A_6, B_5);
  xor xor_1 (Y_6, A_7, B_6);
  xor xor_2 (SUM, A, B);
  and and_2 (CARRY, A, B);
  xor xor_3 (xor_3_out, A_3, B_3);
  and and_3 (and_3_out, A_3, B_3);
  and and_4 (and_4_out, B_3, C);
  and and_5 (and_5_out, C, A_3);
  xor xor_4 (SUM_2, xor_3_out, C);
  or or_2 (or_2_out, and_3_out, and_4_out);
  or or_3 (CARRY_2, or_2_out, and_5_out);

  // Notes on the sheet:
  //   A
  //   B
  //   BASIC GATES
  //   AND GATE
  //   OR GATE
  //   NOT GATE 
  //   NAND GATE
  //   NOR GATE
  //   XOR GATE
  //   HALF ADDER
  //   FULL ADDER
endmodule
